# Fritzing sketch Arduino_SerialCommunication (saved by Fritzing 0.9.3b)
breadboards: 1

parts:
  R1 = Resistor [tolerance=±5% resistance=1k package="1206 [SMD]"]
  R3 = Resistor [tolerance=±5% resistance=1k package="1206 [SMD]"]
  R4 = Resistor [tolerance=±5% resistance=100k package="1206 [SMD]"]
  LED1 = LED - 3mm [color="Green (555nm)" package="3 mm [THT]"]
  LED2 = LED - 3mm [color="Yellow (585nm)" package="3 mm [THT]"]
  LED3 = LED - 3mm [color="Red (633nm)" package="3 mm [THT]"]
  R2 = Resistor [tolerance=±5% resistance=1k package="1206 [SMD]"]
  S1 = SWITCH-MOMENTARY-2 [package=tactile-pth]
  Componente1 = DeuLigne 1.1 - The Snootlab's LCD shield for Arduino

nets:
  N1: R1.Pin_0, R3.Pin_0, R4.Pin_0, R2.Pin_0
  N2: R1.Pin_1, LED1.cathode
  N3: R3.Pin_1, LED3.cathode
  N4: R4.Pin_1, S1.2, Componente1.D12_MISO
  N5: LED1.anode, Componente1.D11_MOSI
  N6: LED2.cathode, R2.Pin_1
  N7: LED2.anode, Componente1.D3
  N8: LED3.anode, Componente1.D4
  N9: S1.1, Componente1.+5V
